# Fritzing sketch Pipettor (saved by Fritzing 0.9.3b)

parts:
  Adafruit_Motor_Shield = Adafruit Motor/Stepper/Servo Shield [part_number="Adafruit #1438"]
  Pipettor_Slide_Pot = Slide Potentiometer [maximum_resistance=10kΩ]
  Pipettor_180_1_Gearmotor = DC Motor

nets:
  N1: Adafruit_Motor_Shield.M1B, Pipettor_180_1_Gearmotor.pin_1
  N2: Adafruit_Motor_Shield.M1A, Pipettor_180_1_Gearmotor.pin_2
  GND: Adafruit_Motor_Shield.GND, Pipettor_Slide_Pot.wiper
  N3: Adafruit_Motor_Shield.+5V, Pipettor_Slide_Pot.leg1
  N4: Adafruit_Motor_Shield.AD0, Pipettor_Slide_Pot.leg2

custom parts:
  Adafruit Motor/Stepper/Servo Shield: The original Adafruit Motorshield kit is one of our most beloved kits, which is why we decided to make something even better. We have upgraded the shield kit to make the bestest, easiest way to drive DC and Stepper motors. This shield will make quick work of your next robotics project! We kept the ability to drive up to 4 DC motors or 2 stepper motors, but added many improvements: Instead of a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
